# Fritzing sketch Esquemático_Fritzing (saved by Fritzing 0.9.3b)
breadboards: 2

parts:
  Part1 = Arduino Mega 2560 (Rev3)
  Part2 = MicroSD Card Module
  LED1 = smd LED [color="White (8000K)" package="0805 [SMD]"]
  LED2 = smd LED [color="White (8000K)" package="0805 [SMD]"]
  LED3 = smd LED [color="White (8000K)" package="0805 [SMD]"]
  LED4 = smd LED [color="White (8000K)" package="0805 [SMD]"]
  LED5 = smd LED [color="White (8000K)" package="0805 [SMD]"]
  LED6 = smd LED [color="White (8000K)" package="0805 [SMD]"]
  LED7 = smd LED [color="White (8000K)" package="0805 [SMD]"]
  LED8 = smd LED [color="White (8000K)" package="0805 [SMD]"]  # not connected
  R1 = Resistor [tolerance=±5% resistance=500 package="0805 [SMD]"]
  R2 = Resistor [tolerance=±5% resistance=500 package="0805 [SMD]"]
  R3 = Resistor [tolerance=±5% resistance=500 package="0805 [SMD]"]
  R5 = Resistor [tolerance=±5% resistance=500 package="0805 [SMD]"]
  R6 = Resistor [tolerance=±5% resistance=500 package="0805 [SMD]"]
  R7 = Resistor [tolerance=±5% resistance=500 package="0805 [SMD]"]
  R8 = Resistor [tolerance=±5% resistance=10k package="0805 [SMD]"]
  S1 = Momentary Switch [package=ksa_sealed_tac_switch]
  S2 = Momentary Switch [package=ksa_sealed_tac_switch]
  R4 = Resistor [tolerance=±5% resistance=500 package="0805 [SMD]"]
  Part3 = Solar Cell
  U1 = LM386 [package=dip08]
  C1 = Electrolytic Capacitor [capacitance=10μF package="0605 [SMD, electrolytic]"]
  R9 = Rotary Potentiometer (Small) [maximum_resistance=10kΩ package=THT]  # not connected
  DC3_9V = Power plug
  C2 = Electrolytic Capacitor [capacitance=10μF package="0605 [SMD, electrolytic]"]
  R10 = Resistor [tolerance=±5% resistance=10 package="0805 [SMD]"]
  C6 = Ceramic Capacitor [capacitance="100 nF" package="0805 [SMD, multilayer]"]
  SPKR1 = Loudspeaker
  C8 = Ceramic Capacitor [capacitance=0.22mF package="1206 [SMD, multilayer]"]
  R13 = Resistor [tolerance=±5% resistance=10k package="0805 [SMD]"]

nets:
  5V: Part1.5V, Part2.VCC, R1.Pin_1, R2.Pin_1, R3.Pin_1, R5.Pin_1, R6.Pin_1, R7.Pin_1, R8.Pin_1, R4.Pin_1, R13.Pin_1
  GND: Part1.GND, Part1.D46, Part2.GND, LED1.cathode, LED2.cathode, LED3.cathode, LED4.cathode, LED5.cathode, LED6.cathode, LED7.cathode, S1.1, S2.1
  N1: Part1.D2_PWM, S1.3
  N2: Part1.D3_PWM, S2.3
  N3: Part1.D50, Part2.MISO
  N4: Part1.D51, Part2.MOSI
  N5: Part1.D52, Part2.SCK
  N6: Part1.D53, Part2.CS
  N7: LED1.anode, R4.Pin_0
  N8: LED2.anode, R5.Pin_0
  N9: LED3.anode, R6.Pin_0
  N10: LED4.anode, R7.Pin_0
  N11: LED6.anode, R3.Pin_0
  N12: LED7.anode, R2.Pin_0
  N13: R8.Pin_0, S1.4
  N14: S2.4, R13.Pin_0
  N15: Part3.+, C1.-
  N16: Part3.-, U1.-IN, U1.V-, DC3_9V.GND, R10.Pin_0, SPKR1.pin1
  N17: U1.GAIN, C2.-
  N18: R10.Pin_1, C6.1
  N19: C6.0, C8.0
  N20: SPKR1.pin2, C8.1

// code stored in the sketch: PlayerWAV_PI.ino
/*
Arduino - Music Player
El circuito:
 * Pulsador - pin 2 and 3
 * Salida de audio - pin 46
 * Conexión SPI del módulo SD: 
 ** MOSI - pin 51
 ** MISO - pin 50
 ** SCK - pin 52
 ** CS - pin 53 
 */
 
#include "SD.h" //Librería para leer la tarjeta de memoria
#include "TMRpcm.h" //Librería para reproducir el audio
#include "SPI.h" //Librería SPI para la tarjeta de memoria

#define SD_ChipSelectPin 53 //Pin para seleción de chip - CS ( Chip Selection )

TMRpcm music; //Objeto llamado "music"

int Bt1 = 0; 
int Bt2 = 0;
boolean db1=true;
boolean db2=true;

void setup()
{

music.speakerPin = 46; //Salida de audio
Serial.begin(9600); //Serial Com para la depuración
if (!SD.begin(SD_ChipSelectPin)) {
Serial.println("SD fail");
return;
}
 pinMode(2,INPUT);  //Definir 2 como entrada digital.
 pinMode(3,INPUT);  //Definir 3 como entrada digital.
 
music.setVolume(7);    //   0 to 7. Establecer el nivel de volumen
music.quality(0);        //  Defini 1 para 2x sobremuestreo y 0 para normal
 
}



void loop()
{ 
  
  Bt1=digitalRead(2); 
  Bt2=digitalRead(3);

 
 if (Bt1 == LOW & db1 == true)  //Para Bt1 presionado, reproduce el archivo "1.wav"
    { 
      {music.play("1");}
      db1 = false;
      Serial.println("Bt1 presionado");
      
    
    }    
    if(Bt2 == LOW & db1 == true) //Para Bt2 presionado, reproduce el archivo "2.wav"
    { 
      {music.play("2");}
      db2 = false;
      Serial.println("Bt2 presionado");
    
    }

   if (digitalRead(2)==HIGH) // Evitar rebotes
  db1=true;

  if (digitalRead(3)==HIGH)  // Evitar rebotes
  db2=true;
}
